// Logisim project Adder_Subtractor_Circuits.circ as structural Verilog: 6 circuits, main circuit main
module main (
  input  a,
  input  b,
  input  Cin_Bin,
  input  in_4,
  output S,
  output S_2,
  output S_D,
  output Cout_Bout,
  output Cout,
  output Cout_2,
  output D,
  output D_2,
  output Bout,
  output Bout_2
);

  Half_Adder half_adder_1 (.a(a), .b(b), .Sum(S), .Cout(Cout));
  Half_Subtractor half_subtractor_1 (.a(a), .b(b), .Difference(D), .Bout(Bout));
  Full_Adder full_adder_1 (.a(a), .b(b), .Cin(Cin_Bin), .Sum(S_2), .Cout(Cout_2));
  Full_Subtractor full_subtractor_1 (.a(a), .b(b), .Bin(Cin_Bin), .Difference(D_2), .Bout(Bout_2));
  Adder_and_Subtractor adder_and_subtractor_1 (
    .a(a), .b(b), .Cin_Bout(Cin_Bin), .in_3(in_4), .Sum_Difference(S_D), .Cout_Bout(Cout_Bout));
endmodule

module Half_Adder (
  input  a,
  input  b,
  output Sum,
  output Cout
);

  xor xor_1 (Sum, a, b);
  and and_1 (Cout, a, b);
endmodule

module Half_Subtractor (
  input  a,
  input  b,
  output Difference,
  output Bout
);

  wire not_1_out;

  not not_1 (not_1_out, a);
  xor xor_1 (Difference, a, b);
  and and_1 (Bout, not_1_out, b);
endmodule

module Full_Adder (
  input  a,
  input  b,
  input  Cin,
  output Sum,
  output Cout
);

  wire and_1_out, and_2_out, xor_1_out;

  xor xor_1 (xor_1_out, a, b);
  and and_1 (and_1_out, a, b);
  xor xor_2 (Sum, xor_1_out, Cin);
  and and_2 (and_2_out, xor_1_out, Cin);
  or or_1 (Cout, and_2_out, and_1_out);
endmodule

module Full_Subtractor (
  input  a,
  input  b,
  input  Bin,
  output Difference,
  output Bout
);

  wire and_1_out, and_2_out, not_1_out, not_2_out, xor_1_out;

  not not_1 (not_1_out, a);
  xor xor_1 (xor_1_out, a, b);
  and and_1 (and_1_out, not_1_out, b);
  xor xor_2 (Difference, xor_1_out, Bin);
  not not_2 (not_2_out, xor_1_out);
  and and_2 (and_2_out, not_2_out, Bin);
  or or_1 (Bout, and_2_out, and_1_out);
endmodule

module Adder_and_Subtractor (
  input  a,
  input  b,
  input  in_3,
  input  Cin_Bout,
  output Sum_Difference,
  output Cout_Bout
);

  wire and_1_out, and_2_out, xor_1_out, xor_2_out;

  xor xor_1 (xor_1_out, in_3, b);
  xor xor_2 (xor_2_out, a, xor_1_out);
  and and_1 (and_1_out, a, xor_1_out);
  xor xor_3 (Sum_Difference, xor_2_out, Cin_Bout);
  and and_2 (and_2_out, xor_2_out, Cin_Bout);
  or or_1 (Cout_Bout, and_2_out, and_1_out);
endmodule
